# Fritzing sketch FERG (saved by Fritzing 0.9.1b)
circuit board: 8.46667cm x 5.64444cm
breadboards: 1

parts:
  U6 = 3.5mm Audio Jack [package=audio-jack-3.5mm-smd]
  U7 = 3.5mm Audio Jack [package=audio-jack-3.5mm-smd]
  U8 = 3.5mm Audio Jack [package=audio-jack-3.5mm-smd]
  U9 = 3.5mm Audio Jack [package=audio-jack-3.5mm-smd]
  U10 = 3.5mm Audio Jack [package=audio-jack-3.5mm-smd]
  U11 = 3.5mm Audio Jack [package=audio-jack-3.5mm-smd]
  IC1 = MCP3008 8-channel 10-bit ADC [part_number=MCP3008]
  Raspberry_Pi1 = Raspberry Pi B+
  J1 = Screw terminal - 2 pins [package=THT]
  J2 = Screw terminal - 2 pins [package=THT]
  Relais = female pin header, 6 pins [form="♀ (female)"]
  433_Mhz = female pin header, 4 pins [form="♀ (female)"]
  SG1 = Buzzer 12mm [package=buzzer-12mm-ns-kit]
  LED1 = LED - 5mm [color="White (4500K)" package="5 mm [THT]"]
  R1 = Resistor [tolerance=±5% resistance=220 package=THT]
  R2 = Resistor [tolerance=±5% resistance=100 package=THT]
  R3 = Resistor [tolerance=±5% resistance=1k package=THT]
  J3 = Screw terminal - 2 pins [package=THT]

nets:
  N1: U6.SLEEVE, IC1.CH6
  N2: U6.LEFT, U8.SLEEVE, U9.LEFT, U10.LEFT, U11.LEFT, IC1.CH4, IC1.DGND, IC1.Dout, IC1.AGND, Raspberry_Pi1.GND, Raspberry_Pi1.GIPO9, J1.pin2, J2.pin1, Relais.pin6, 433_Mhz.pin4, SG1.2, R3.Pin_1, J3.pin2
  N3: U7.SLEEVE, IC1.CH5
  N4: U9.SLEEVE, IC1.CH3
  N5: U10.SLEEVE, IC1.CH2
  N6: U11.SLEEVE, IC1.CH1
  N7: IC1.CH0, J2.pin2, R2.Pin_0
  N8: IC1.CS, Raspberry_Pi1.GIPO8
  N9: IC1.Din, Raspberry_Pi1.GIPO10
  N10: IC1.CLK, Raspberry_Pi1.GIPO11
  N11: IC1.Vref, Raspberry_Pi1.3V3, R2.Pin_1
  VDD: IC1.Vdd, Raspberry_Pi1.5V, Relais.pin1, 433_Mhz.pin1, R1.Pin_1
  N12: Raspberry_Pi1.GIPO4, 433_Mhz.pin3
  N13: Raspberry_Pi1.GIPO16, LED1.anode
  N14: Raspberry_Pi1.GIPO25, SG1.1
  N15: Raspberry_Pi1.GIPO24, J3.pin1
  N16: Raspberry_Pi1.GIPO23, Relais.pin2
  N17: J1.pin1, R1.Pin_0
  N18: LED1.cathode, R3.Pin_0

custom parts:
  Raspberry Pi B+: The awesome Raspberry Pi ARM Board with 40 pin gipo. Ready for special designed Raspberry Pi B+ Hat (Hardware attached (on) top)
