# Fritzing sketch arduino (saved by Fritzing 0.9.1b)
breadboards: 1

parts:
  Composant1 = Arduino Nano (Rev3.0)
  LED1 = LED - 5mm [color="Yellow (595nm)" package="5 mm [THT]"]
  R1 = Resistor [tolerance=±5% resistance=10k package=THT]
  J1 = Screw terminal - 2 pins [package=THT]
  J2 = Screw terminal - 2 pins [package=THT]
  J3 = Screw terminal - 2 pins [package=THT]
  J4 = Screw terminal - 2 pins [package=THT]
  R2 = Resistor [tolerance=±5% resistance=10k package=THT]
  R3 = Resistor [tolerance=±5% resistance=100 package=THT]
  Raspberry_Pi2 = Raspberry Pi B+
  U1 = QRD1114 [package=qrd1114]

nets:
  N1: Composant1.GND, R1.Pin_0
  N2: Composant1.D8, LED1.anode
  VIN: Composant1.VIN, J3.pin1, R2.Pin_0, R3.Pin_0, Raspberry_Pi2.5V
  N3: Composant1.A5, J4.pin2, Raspberry_Pi2.GPIO3
  N4: Composant1.A4, J4.pin1, Raspberry_Pi2.GPIO2
  N5: Composant1.A0, J1.pin2, R2.Pin_1, U1.C
  N6: LED1.cathode, R1.Pin_1
  N7: J1.pin1, J2.pin2, J3.pin2, Raspberry_Pi2.GND, U1.E, U1.A
  N8: J2.pin1, R3.Pin_1, U1.K

custom parts:
  Raspberry Pi B+: The awesome Raspberry Pi ARM Board with 40 pin gipo. Ready for special designed Raspberry Pi B+ Hat (Hardware attached (on) top)
