# Fritzing sketch carte 2 cateurs temperature et WIFI (saved by Fritzing 0.9.1b)
circuit board: 8.46667cm x 5.64444cm
breadboards: 1

parts:
  DS1820_n°1 = Header 4 [package=molex-1x4_lock]
  DS1820_n°2 = Header 4 [package=molex-1x4_lock]
  R1 = Resistor [tolerance=±5% resistance=4.7k package=THT]
  TTL_to_USB = Header 4 [package=molex-1x4_lock]
  S3 = Pushbutton [package="[SMD]"]
  J1 = Power Jack [package=power_jack_smd]
  U1 = ESP8266 WiFi Module [part_number=ESP8266]

nets:
  GND: DS1820_n°1.1, DS1820_n°2.1, TTL_to_USB.1, S3.Pin_3, S3.Pin_4, J1.GND, U1.GND
  N1: DS1820_n°1.2, DS1820_n°2.2, R1.Pin_0, J1.PWR, U1.VCC, U1.CH_PD
  N2: DS1820_n°1.4, DS1820_n°2.4, R1.Pin_1, U1.GPIO_2
  N3: TTL_to_USB.3, U1.RXD
  N4: TTL_to_USB.4, U1.TXD
  N5: S3.Pin_2, U1.GPIO_0

custom parts:
  ESP8266 WiFi Module: Generic WiFi Module based on the ESP8266 with onboard PCB antenna and UART communications
