# Fritzing sketch carte tableau electrique2 (saved by Fritzing 0.9.1b)
circuit board: 8.46667cm x 5.64444cm
breadboards: 1

parts:
  U1 = 3.5mm Audio Jack [package=audio-jack-3.5mm-smd]
  U2 = 3.5mm Audio Jack [package=audio-jack-3.5mm-smd]
  U3 = 3.5mm Audio Jack [package=audio-jack-3.5mm-smd]
  U4 = 3.5mm Audio Jack [package=audio-jack-3.5mm-smd]
  U5 = 3.5mm Audio Jack [package=audio-jack-3.5mm-smd]
  U6 = 3.5mm Audio Jack [package=audio-jack-3.5mm-smd]
  U8 = RJ45 Jack [package=rj45-8]
  R4 = Resistor [tolerance=±5% resistance=680k package=THT]
  C3 = Capacitor [package=cap-pth-large]
  D2 = Diode [package=diode-1n4148]
  C4 = Electrolytic Capacitor [capacitance=100µF voltage=20V package="200 mil [THT, electrolytic]"]
  U9 = TLP621 [package=THT]
  R3 = Resistor [tolerance=±5% resistance=100 package=THT]
  JP1 = Header 2 [package=screwterminal-3.5mm-2_lock]
  IC1 = MCP3008 8-channel 10-bit ADC [part_number=MCP3008]  # not connected

nets:
  N1: U1.SLEEVE, U2.SLEEVE, U3.SLEEVE, U4.SLEEVE, U5.SLEEVE, U6.SLEEVE, U8.8, U9.Pin_3
  N2: U1.LEFT, U8.5
  N3: U2.LEFT, U8.3
  N4: U3.LEFT, U8.1
  N5: U4.LEFT, U8.2
  N6: U5.LEFT, U8.4
  N7: U6.LEFT, U8.6
  N8: U8.7, U9.Pin_4
  N9: R4.Pin_0, C3.1, R3.Pin_0
  N10: R4.Pin_1, C3.2, D2.A
  N11: D2.C, C4.+
  N12: C4.-, U9.Pin_1
  N13: U9.Pin_2, JP1.2
  N14: R3.Pin_1, JP1.1
