# Fritzing sketch detecteur de tension (saved by Fritzing 0.9.1b)
circuit board: 8.46667cm x 5.64444cm
breadboards: 1

parts:
  R1 = Resistor [tolerance=±5% resistance=100 package=THT]  # not connected
  R2 = Resistor [tolerance=±5% resistance=680k package=THT]
  C1 = Capacitor [package=cap-pth-large]
  U1 = TLP621 [package=THT]
  Pad1 = Pad [width=2.91202502020202 height=3.90493421818182 connect=center]  # not connected
  Pad2 = Pad [width=2.91202502020202 height=3.90493421818182 connect=center]
  Pad3 = Pad [width=2.91202502020202 height=3.90493421818182 connect=center]
  Pad4 = Pad [width=2.91202502020202 height=3.90493421818182 connect=center]
  C2 = Electrolytic Capacitor [capacitance=100µF voltage=20V package="200 mil [THT, electrolytic]"]
  D1 = Diode [package=diode-1n4148]

nets (from the pcb view):
  N1: R2.Pin_0, C1.1
  N2: R2.Pin_1, C1.2, D1.A
  N3: U1.Pin_1, C2.-
  N4: U1.Pin_2, Pad2.pad
  N5: U1.Pin_4, Pad4.pad
  N6: U1.Pin_3, Pad3.pad
  N7: C2.+, D1.C
